# Fritzing sketch dpf-bt (saved by Fritzing 0.9.6b)
breadboards: 1

parts:
  LCD2004-I2C2 = LCD2004-I2C
  Bauteil1 = Solid State High Level Relay Module [package=relay]
  R1 = Resistor [tolerance=±5% resistance=1k package="0402 [SMD]"]
  R3 = Resistor [tolerance=±5% resistance=100 package="0402 [SMD]"]
  On_-_Auto_-_Off = Slide_SW_micro_dpdt
  R4 = Resistor [tolerance=±5% resistance=100 package="0402 [SMD]"]
  C3 = Capacitor Polarized [package=cpol-radial-1000uf-25v]
  C4 = Ceramic Capacitor [capacitance=100nF voltage=35V package="200 mil [THT, multilayer]"]
  MCU1 = Raspberry Pi Zero

nets:
  N1: LCD2004-I2C2.GND, Bauteil1.DC-, R4.Pin_1, C3.-, C4.0, MCU1.pin_6, MCU1.pin_9, MCU1.pin_34
  N2: LCD2004-I2C2.VCC, Bauteil1.DC+, R3.Pin_1, C3.+, C4.1, MCU1.pin_2, MCU1.pin_4
  N3: LCD2004-I2C2.SDA, MCU1.pin_3
  N4: LCD2004-I2C2.SCL, MCU1.pin_5
  N5: Bauteil1.CH1, R1.Pin_1, On_-_Auto_-_Off.pin_1, MCU1.pin_11
  N6: R1.Pin_0, MCU1.pin_22
  N7: R3.Pin_0, On_-_Auto_-_Off.pin_2
  N8: On_-_Auto_-_Off.pin_3, R4.Pin_0

custom parts:
  LCD2004-I2C: A standard character display with 4x20 characters. Comes in many colors with LCM2004 IIC attached.
  Solid State High Level Relay Module: 5V Omron solid state relay 240V 2A output with resistance fuse.
  Slide_SW_micro_dpdt: silver mico switch
